# Fritzing sketch PixelBotPCB_V2_Final (saved by Fritzing 0.9.3b)
circuit board: 8.5cm x 8.5cm

parts:
  L293D-B = L293D [package=THT]
  L293D-A = L293D [package=THT]
  MTR-U = female pin header, 6 pins [form="♀ (female)"]
  MTR-L = female pin header, 6 pins [form="♀ (female)"]
  MTR-R = female pin header, 6 pins [form="♀ (female)"]
  D2 = Diode [package=diode-1n4001]
  C2 = Capacitor [package=cap-pth-small2]
  C4 = Capacitor [package=cap-pth-small2]
  EC2 = Electrolytic Capacitor [capacitance=1µF package="100 mil [THT, electrolytic]"]
  EC4 = Electrolytic Capacitor [capacitance=1µF package="100 mil [THT, electrolytic]"]
  C1 = Capacitor [package=cap-pth-small2]
  EC1 = Electrolytic Capacitor [capacitance=1µF package="100 mil [THT, electrolytic]"]
  C3 = Capacitor [package=cap-pth-small2]
  EC3 = Electrolytic Capacitor [capacitance=1µF package="100 mil [THT, electrolytic]"]
  HC-05 = Bluetooth HC-05 Macho
  D1 = Diode [package=diode-1n4001]
  DC = Power Jack [package=power_jack_slot]
  MTR-D = female pin header, 6 pins [form="♀ (female)"]
  MPU = GY-521 (MPU-6050) [form="♀ (female)" package=THT]
  NANO = Arduino Nano (Rev3.0) (ICSP)
  RGB = RGB LED - (4 legs) [package="5 mm [THT]"]
  7805 = Voltage Regulator [package=to-220-alt]

nets (from the pcb view):
  N1: L293D-B.Enable_1, NANO.D6
  N2: L293D-B.In_1, L293D-B.In_4, NANO.D7
  N3: L293D-B.Out_1_(_Controlled_by_Enable_1_), MTR-D.pin6
  GND: L293D-B.0V, L293D-A.0V, MTR-U.pin2, MTR-L.pin2, MTR-R.pin2, C2.1, C4.1, EC2.-, EC4.-, C1.2, EC1.-, C3.2, EC3.-, HC-05.GND, DC.GNDBREAK, DC.GND, MTR-D.pin2, MPU.pin2, NANO.GND, RGB.common_anode, 7805.GND
  N4: L293D-B.Out_2_(_Controlled_by_Enable_1_), MTR-D.pin1
  N5: L293D-B.In_2, L293D-B.In_3, NANO.D8
  N6: L293D-B.+Vmotor, L293D-A.+Vmotor, C2.2, C4.2, EC2.+, EC4.+, D1.C
  N7: L293D-B.Enable_2, NANO.D9
  N8: L293D-B.Out_3_(_Controlled_by_Enable_2_), MTR-U.pin6
  N9: L293D-B.Out_4_(_Controlled_by_Enable_2_), MTR-U.pin1
  N10: L293D-B.+V, L293D-A.+V, MTR-U.pin5, MTR-L.pin5, MTR-R.pin5, C1.1, EC1.+, C3.1, EC3.+, MTR-D.pin5, 7805.IN
  N11: L293D-A.Enable_1, NANO.D5
  N12: L293D-A.In_1, L293D-A.In_4, NANO.D11/MOSI
  N13: L293D-A.Out_1_(_Controlled_by_Enable_1_), MTR-L.pin6
  N14: L293D-A.Out_2_(_Controlled_by_Enable_1_), MTR-L.pin1
  N15: L293D-A.In_2, L293D-A.In_3, NANO.D12/MISO
  N16: L293D-A.Enable_2, NANO.D3
  N17: L293D-A.Out_3_(_Controlled_by_Enable_2_), MTR-R.pin6
  N18: L293D-A.Out_4_(_Controlled_by_Enable_2_), MTR-R.pin1
  N19: MTR-U.pin4, NANO.A6
  N20: MTR-L.pin4, NANO.A3
  N21: MTR-R.pin4, NANO.D13/SCK
  N22: D2.A, DC.PWR, NANO.VIN, 7805.OUT
  N23: D2.C, D1.A
  N24: HC-05.TXD, NANO.D4
  N25: HC-05.RXD, NANO.D10
  VCC: HC-05.VCC, NANO.3V3
  N26: MTR-D.pin4, NANO.A7
  N27: MPU.pin1, NANO.5V
  N28: MPU.pin3, NANO.A5
  N29: MPU.pin4, NANO.A4
  N30: MPU.pin5, NANO.D2
  N31: NANO.A2, RGB.blue_cathode
  N32: NANO.A1, RGB.green_cathode
  N33: NANO.A0, RGB.red_cathode

notes:
  Bluetooth module
  6x NiMH batteries
  RGB LED disc
  IMU sensor
  2x motor drivers and voltage regulator
  Arduino nano
  Pixelbot v2
  M+
  5V
  EA
  EB
  GND
  M-

custom parts:
  GY-521 (MPU-6050): Placa GY-521 basada en conjunto de acelerómetro+giroscopios MPU-6050
